# Fritzing sketch Wiring Diagram (saved by Fritzing 0.9.3b)
breadboards: 1

parts:
  Part1 = Arduino Uno (Rev3)
  R1 = Rotary Potentiometer (Small) [maximum_resistance=100kΩ package=THT]
  T1 = LM35 Temperature Sensor [package="TO92 [THT]"]
  S1 = Pushbutton [package="[THT]"]
  S2 = Pushbutton [package="[THT]"]
  IC1 = A4950 [package=soicn]
  M1 = Stepper Motor - Bipolar

nets:
  N1: Part1.D8, IC1.VBB
  N2: Part1.D9_PWM, IC1.OUT1
  N3: Part1.D10_PWM/SS, IC1.LSS
  N4: Part1.D11_PWM/MOSI, IC1.OUT2
  N5: Part1.D5_PWM, T1.Vout
  N6: Part1.D6_PWM, S2.Pin_3, S2.Pin_4
  N7: Part1.D7, S1.Pin_3, S1.Pin_4
  N8: Part1.5V, R1.leg1, T1.+Vs
  GND: Part1.GND, R1.leg2, T1.GND, S1.Pin_1, S1.Pin_2, S2.Pin_1, S2.Pin_2
  N9: IC1.GND, M1.D
  N10: IC1.IN2, M1.B
  N11: IC1.IN1, M1.C
  N12: IC1.VREF, M1.A
